# Fritzing sketch ShutterGlasses (saved by Fritzing 0.6.3b)
breadboards: 1

parts:
  U1 = LM 358 Dual Op-Amp [package="DIP8 [THT]"]
  U2 = LM 358 Dual Op-Amp [package="DIP8 [THT]"]
  R1 = Resistor [resistance=15k tolerance=±5% package=THT]
  R2 = Resistor [resistance=15k tolerance=±5% package=THT]
  R3 = Resistor [resistance=15k tolerance=±5% package=THT]
  R4 = Resistor [resistance=15k tolerance=±5% package=THT]
  IC1 = IC, DIP package, 8 pins [chip_label=LT1301 spacing=300mil]
  L1 = Inductor [inductance=33µ package="400 mil [THT]"]
  D1 = Schottky Diode [part_number=1N5817 package="300 mil [THT]"]
  C1 = Ceramic Capacitor [capacitance=100nF package="200 mil [THT, multilayer]"]
  C2 = Electrolytic Capacitor [capacitance=47µF voltage=20V package="100 mil [THT, electrolytic]"]
  C3 = Electrolytic Capacitor [capacitance=47µF voltage=20V package="100 mil [THT, electrolytic]"]
  TRS1 = Stereo Jack (TRS) 3.5mm [package="PG203J [THT]"]
  Arduino1 = Arduino Fio

nets:
  N1: U1.connector3, U2.connector3, R2.Pin_1, R4.Pin_1, IC1.pin1, IC1.pin8, C1.0, C2.-, C3.-, TRS1.Sleeve, Arduino1.GND
  N2: U1.connector4, U2.connector5, R1.Pin_0, R2.Pin_0
  N3: U1.connector5, U2.connector4, Arduino1.D4
  N4: U1.connector6, R4.Pin_0, TRS1.Tip
  N5: U1.connector7, U2.connector7, IC1.pin4, D1.cathode, C1.1, C3.+
  N6: U2.connector6, R3.Pin_0, TRS1.Ring
  N7: R1.Pin_1, R3.Pin_1, IC1.pin2, IC1.pin6, L1.pin_1, C2.+, Arduino1.3V3
  N8: IC1.pin7, L1.pin_0, D1.anode
